// Logisim project 8-Bit CPU V2.circ as structural Verilog
module ALU (
  input  [7:0] A,
  input  [7:0] B,
  input  ADC,
  input  CIN,
  input  [2:0] OP,
  output S,
  output V,
  output N,
  output C,
  output [7:0] OUT,
  output Z
);

  wire and_1_out, and_2_out, and_3_out, and_4_out, and_5_out, and_6_out, and_7_out, and_8_out, and_9_out,
       B_0_out, Cin_out, DEC_out, INC_out, INVC_out, n1_bit_alu_1_c_out, n1_bit_alu_2_c_out,
       n1_bit_alu_3_c_out, n1_bit_alu_4_c_out, n1_bit_alu_5_c_out, n1_bit_alu_6_c_out, n1_bit_alu_7_c_out,
       n1_bit_alu_8_c_out, SUB_2_out, SUB_out, xor_1_out, xor_2_out, xor_3_out, xor_4_out, xor_5_out,
       xor_6_out, xor_7_out, xor_8_out;
  wire [7:0] n1_bit_alu_8_and, n1_bit_alu_8_not, n1_bit_alu_8_or, n1_bit_alu_8_sum, n1_bit_alu_8_xor;

  and and_1 (and_1_out, ADC, CIN);
  and INC (INC_out, OP[2], OP[1], OP[0]);
  and SUB (SUB_out, ~OP[2], ~OP[1], OP[0]);  // AND_Gate
  or B_0 (B_0_out, INC_out, DEC_out);
  or SUB_2 (SUB_2_out, SUB_out, DEC_out);
  or u_Cin (Cin_out, and_1_out, INC_out, DEC_out);
  and DEC (DEC_out, OP[2], OP[1], ~OP[0]);  // AND_Gate
  xor xor_1 (xor_1_out, SUB_2_out, B[7]);
  and and_2 (and_2_out, ~B_0_out, xor_1_out);  // AND_Gate
  _1_Bit_ALU u_1_bit_alu_1 (
    .A(A[7]), .B(and_2_out), .C_in(n1_bit_alu_2_c_out), .NOT(n1_bit_alu_8_not[7]), .AND(n1_bit_alu_8_and[7]),
    .OR(n1_bit_alu_8_or[7]), .XOR(n1_bit_alu_8_xor[7]), .SUM(n1_bit_alu_8_sum[7]), .C_OUT(n1_bit_alu_1_c_out));
  xor xor_2 (xor_2_out, SUB_2_out, B[6]);
  and and_3 (and_3_out, ~B_0_out, xor_2_out);  // AND_Gate
  _1_Bit_ALU u_1_bit_alu_2 (
    .A(A[6]), .B(and_3_out), .C_in(n1_bit_alu_3_c_out), .NOT(n1_bit_alu_8_not[6]), .AND(n1_bit_alu_8_and[6]),
    .OR(n1_bit_alu_8_or[6]), .XOR(n1_bit_alu_8_xor[6]), .SUM(n1_bit_alu_8_sum[6]), .C_OUT(n1_bit_alu_2_c_out));
  xor xor_3 (xor_3_out, SUB_2_out, B[5]);
  and and_4 (and_4_out, ~B_0_out, xor_3_out);  // AND_Gate
  _1_Bit_ALU u_1_bit_alu_3 (
    .A(A[5]), .B(and_4_out), .C_in(n1_bit_alu_4_c_out), .NOT(n1_bit_alu_8_not[5]), .AND(n1_bit_alu_8_and[5]),
    .OR(n1_bit_alu_8_or[5]), .XOR(n1_bit_alu_8_xor[5]), .SUM(n1_bit_alu_8_sum[5]), .C_OUT(n1_bit_alu_3_c_out));
  xor xor_4 (xor_4_out, SUB_2_out, B[4]);
  and and_5 (and_5_out, ~B_0_out, xor_4_out);  // AND_Gate
  _1_Bit_ALU u_1_bit_alu_4 (
    .A(A[4]), .B(and_5_out), .C_in(n1_bit_alu_5_c_out), .NOT(n1_bit_alu_8_not[4]), .AND(n1_bit_alu_8_and[4]),
    .OR(n1_bit_alu_8_or[4]), .XOR(n1_bit_alu_8_xor[4]), .SUM(n1_bit_alu_8_sum[4]), .C_OUT(n1_bit_alu_4_c_out));
  xor xor_5 (xor_5_out, SUB_2_out, B[3]);
  and and_6 (and_6_out, ~B_0_out, xor_5_out);  // AND_Gate
  _1_Bit_ALU u_1_bit_alu_5 (
    .A(A[3]), .B(and_6_out), .C_in(n1_bit_alu_6_c_out), .NOT(n1_bit_alu_8_not[3]), .AND(n1_bit_alu_8_and[3]),
    .OR(n1_bit_alu_8_or[3]), .XOR(n1_bit_alu_8_xor[3]), .SUM(n1_bit_alu_8_sum[3]), .C_OUT(n1_bit_alu_5_c_out));
  xor xor_6 (xor_6_out, SUB_2_out, B[2]);
  and and_7 (and_7_out, ~B_0_out, xor_6_out);  // AND_Gate
  _1_Bit_ALU u_1_bit_alu_6 (
    .A(A[2]), .B(and_7_out), .C_in(n1_bit_alu_7_c_out), .NOT(n1_bit_alu_8_not[2]), .AND(n1_bit_alu_8_and[2]),
    .OR(n1_bit_alu_8_or[2]), .XOR(n1_bit_alu_8_xor[2]), .SUM(n1_bit_alu_8_sum[2]), .C_OUT(n1_bit_alu_6_c_out));
  xor xor_7 (xor_7_out, SUB_2_out, B[1]);
  and and_8 (and_8_out, ~B_0_out, xor_7_out);  // AND_Gate
  _1_Bit_ALU u_1_bit_alu_7 (
    .A(A[1]), .B(and_8_out), .C_in(n1_bit_alu_8_c_out), .NOT(n1_bit_alu_8_not[1]), .AND(n1_bit_alu_8_and[1]),
    .OR(n1_bit_alu_8_or[1]), .XOR(n1_bit_alu_8_xor[1]), .SUM(n1_bit_alu_8_sum[1]), .C_OUT(n1_bit_alu_7_c_out));
  xor xor_8 (xor_8_out, SUB_2_out, B[0]);
  and and_9 (and_9_out, ~B_0_out, xor_8_out);  // AND_Gate
  _1_Bit_ALU u_1_bit_alu_8 (
    .A(A[0]), .B(and_9_out), .C_in(INVC_out), .NOT(n1_bit_alu_8_not[0]), .AND(n1_bit_alu_8_and[0]),
    .OR(n1_bit_alu_8_or[0]), .XOR(n1_bit_alu_8_xor[0]), .SUM(n1_bit_alu_8_sum[0]), .C_OUT(n1_bit_alu_8_c_out));
  xor INVC (INVC_out, Cin_out, SUB_2_out);
  xor INVC_2 (C, SUB_2_out, n1_bit_alu_1_c_out);
  Multiplexer #(.select(3), .width(8), .enable("false")) multiplexer_1 (
    .in0(n1_bit_alu_8_sum), .in1(n1_bit_alu_8_sum), .in2(n1_bit_alu_8_and), .in3(n1_bit_alu_8_or),
    .in4(n1_bit_alu_8_not), .in5(n1_bit_alu_8_xor), .in6(n1_bit_alu_8_sum), .in7(n1_bit_alu_8_sum),
    .out(OUT), .sel(OP));
  nor nor_1 (Z, OUT[7], OUT[6], OUT[5], OUT[4], OUT[3], OUT[2], OUT[1], OUT[0]);
endmodule

module _1_Bit_ALU (
  input  A,
  input  B,
  input  C_in,
  output NOT,
  output AND,
  output OR,
  output XOR,
  output SUM,
  output C_OUT
);

  not not_1 (NOT, A);
  and and_1 (AND, A, B);
  or or_1 (OR, A, B);
  xor xor_1 (XOR, A, B);
  Adder #(.width(1)) adder_1 (.a(B), .b(A), .out(SUM), .cin(C_in), .cout(C_OUT));
endmodule
